// Logisim project Logisim_file.circ as structural Verilog: 2 circuits, main circuit CS3
module main (
  input  load,
  input  in_2,
  input  in_3,
  input  in_4,
  input  in_5,
  input  [7:0] in_6,
  input  [7:0] in_7,
  input  in_8,
  input  in_9,
  input  in_10,
  input  [7:0] in_11,
  output [16:0] out_12
);

  wire adder_1_cout, and_2_out, bcd_to_7_segment_decoder_1_p1, bcd_to_7_segment_decoder_1_p2,
       bcd_to_7_segment_decoder_1_p3, bcd_to_7_segment_decoder_1_p4, bcd_to_7_segment_decoder_1_p6,
       bcd_to_7_segment_decoder_1_p7, bcd_to_7_segment_decoder_1_p8, bcd_to_7_segment_decoder_2_p1,
       bcd_to_7_segment_decoder_2_p2, bcd_to_7_segment_decoder_2_p3, bcd_to_7_segment_decoder_2_p4,
       bcd_to_7_segment_decoder_2_p6, bcd_to_7_segment_decoder_2_p7, bcd_to_7_segment_decoder_2_p8,
       bcd_to_7_segment_decoder_3_p1, bcd_to_7_segment_decoder_3_p2, bcd_to_7_segment_decoder_3_p3,
       bcd_to_7_segment_decoder_3_p4, bcd_to_7_segment_decoder_3_p6, bcd_to_7_segment_decoder_3_p7,
       bcd_to_7_segment_decoder_3_p8, bcd_to_7_segment_decoder_4_p1, bcd_to_7_segment_decoder_4_p2,
       bcd_to_7_segment_decoder_4_p3, bcd_to_7_segment_decoder_4_p4, bcd_to_7_segment_decoder_4_p6,
       bcd_to_7_segment_decoder_4_p7, bcd_to_7_segment_decoder_4_p8, bcd_to_7_segment_decoder_5_p1,
       bcd_to_7_segment_decoder_5_p2, bcd_to_7_segment_decoder_5_p3, bcd_to_7_segment_decoder_5_p4,
       bcd_to_7_segment_decoder_5_p6, bcd_to_7_segment_decoder_5_p7, bcd_to_7_segment_decoder_5_p8,
       clock_1_out, cs3_1_out_5, cs3_1_out_6, cs3_1_out_7, cs3_1_out_8, cs3_2_out_5, cs3_2_out_6,
       cs3_2_out_7, cs3_2_out_8, cs3_3_out_5, cs3_3_out_6, cs3_3_out_7, cs3_3_out_8, cs3_4_out_5,
       cs3_4_out_6, cs3_4_out_7, cs3_4_out_8, cs3_5_out_5, cs3_5_out_6, cs3_5_out_7, cs3_5_out_8,
       cs3_6_out_5, cs3_6_out_6, cs3_6_out_7, cs3_6_out_8, cs3_7_out_5, cs3_7_out_6, cs3_7_out_7,
       cs3_7_out_8, cs3_8_out_5, cs3_8_out_6, cs3_8_out_7, cs3_8_out_8, cs3_9_out_5, cs3_9_out_6,
       cs3_9_out_7, cs3_9_out_8, cs3_10_out_5, cs3_10_out_6, cs3_10_out_7, cs3_10_out_8, cs3_11_out_5,
       cs3_11_out_6, cs3_11_out_7, cs3_11_out_8, cs3_12_out_5, cs3_12_out_6, cs3_12_out_7, cs3_12_out_8,
       cs3_13_out_5, cs3_13_out_6, cs3_13_out_7, cs3_13_out_8, cs3_14_out_5, cs3_14_out_6, cs3_14_out_7,
       cs3_14_out_8, cs3_15_out_5, cs3_15_out_6, cs3_15_out_7, cs3_15_out_8, cs3_16_out_5, cs3_16_out_6,
       cs3_16_out_7, cs3_16_out_8, cs3_17_out_5, cs3_17_out_6, cs3_17_out_7, cs3_17_out_8, cs3_18_out_5,
       cs3_18_out_6, cs3_18_out_7, cs3_18_out_8, cs3_19_out_5, cs3_19_out_6, cs3_19_out_7, cs3_19_out_8,
       cs3_20_out_5, cs3_20_out_6, cs3_20_out_7, cs3_20_out_8, cs3_21_out_5, cs3_21_out_6, cs3_21_out_7,
       cs3_21_out_8, cs3_22_out_5, cs3_22_out_6, cs3_22_out_7, cs3_22_out_8, cs3_23_out_5, cs3_23_out_6,
       cs3_23_out_7, cs3_23_out_8, cs3_24_out_5, cs3_24_out_6, cs3_24_out_7, cs3_24_out_8, cs3_25_out_5,
       cs3_25_out_6, cs3_25_out_7, cs3_25_out_8, cs3_26_out_5, cs3_26_out_6, cs3_26_out_7, cs3_26_out_8,
       cs3_27_out_5, cs3_27_out_6, cs3_27_out_7, cs3_27_out_8, cs3_28_out_5, cs3_28_out_6, cs3_28_out_7,
       cs3_28_out_8, cs3_29_out_5, cs3_29_out_6, cs3_29_out_7, cs3_29_out_8, cs3_30_out_5, cs3_30_out_6,
       cs3_30_out_7, cs3_30_out_8, cs3_35_out_8, not_1_out, undriven_2;
  wire [3:0] bcd_to_7_segment_decoder_5_p5, cs3_31_out_8, cs3_32_out_8, cs3_33_out_8, cs3_34_out_8;
  wire [7:0] adder_1_out, multiplexer_1_out, multiplexer_2_out;
  wire [15:1] undriven;

  Clock clock_1 (.out(clock_1_out));
  Multiplexer #(.width(8)) multiplexer_1 (.in0(in_6), .in1(in_7), .out(multiplexer_1_out), .sel(in_8));
  Adder adder_1 (.a(out_12[16:9]), .b(multiplexer_1_out), .out(adder_1_out), .cout(adder_1_cout));  // open: cin
  Multiplexer #(.width(8)) multiplexer_2 (.in0(in_11), .in1(out_12[8:1]), .out(multiplexer_2_out), .sel(in_10));
  // Shift_Register #(.length(17)) shift_register_1: pin names not known; wires that end beside it: in_2, load, in_3, in_4, in_5, adder_1_out[7], adder_1_out[6], adder_1_out[5], adder_1_out[4], adder_1_out[3], adder_1_out[2], adder_1_out[1], adder_1_out[0], multiplexer_2_out[7], multiplexer_2_out[6], multiplexer_2_out[5], multiplexer_2_out[4], out_12[15], out_12[14], out_12[13], out_12[12], out_12[11], out_12[10], out_12[9], out_12[8], out_12[7], out_12[6], out_12[5]
  not not_1 (not_1_out, undriven_2);
  // AND_Gate and_1 has open pins: in0=in_9, in1=not_1_out, out=open
  CS3 cs3_1 (
    .in_1(undriven[13]), .in_2(undriven[14]), .in_3(undriven[15]), .in_4(1'b0), .out_5(cs3_1_out_5),
    .out_6(cs3_1_out_6), .out_7(cs3_1_out_7), .out_8(cs3_1_out_8));
  and and_2 (and_2_out, undriven_2, in_9);
  CS3 cs3_2 (
    .in_1(undriven[12]), .in_2(cs3_1_out_5), .in_3(cs3_1_out_6), .in_4(cs3_1_out_7), .out_5(cs3_2_out_5),
    .out_6(cs3_2_out_6), .out_7(cs3_2_out_7), .out_8(cs3_2_out_8));
  CS3 cs3_3 (
    .in_1(undriven[11]), .in_2(cs3_2_out_5), .in_3(cs3_2_out_6), .in_4(cs3_2_out_7), .out_5(cs3_3_out_5),
    .out_6(cs3_3_out_6), .out_7(cs3_3_out_7), .out_8(cs3_3_out_8));
  CS3 cs3_4 (
    .in_1(undriven[9]), .in_2(cs3_5_out_5), .in_3(cs3_5_out_6), .in_4(cs3_5_out_7), .out_5(cs3_4_out_5),
    .out_6(cs3_4_out_6), .out_7(cs3_4_out_7), .out_8(cs3_4_out_8));
  CS3 cs3_5 (
    .in_1(undriven[10]), .in_2(cs3_3_out_5), .in_3(cs3_3_out_6), .in_4(cs3_3_out_7), .out_5(cs3_5_out_5),
    .out_6(cs3_5_out_6), .out_7(cs3_5_out_7), .out_8(cs3_5_out_8));
  CS3 cs3_6 (
    .in_1(cs3_5_out_8), .in_2(cs3_7_out_5), .in_3(cs3_7_out_6), .in_4(cs3_7_out_7), .out_5(cs3_6_out_5),
    .out_6(cs3_6_out_6), .out_7(cs3_6_out_7), .out_8(cs3_6_out_8));
  CS3 cs3_7 (
    .in_1(cs3_3_out_8), .in_2(cs3_2_out_8), .in_3(cs3_1_out_8), .in_4(1'b0), .out_5(cs3_7_out_5),
    .out_6(cs3_7_out_6), .out_7(cs3_7_out_7), .out_8(cs3_7_out_8));
  CS3 cs3_8 (
    .in_1(undriven[8]), .in_2(cs3_4_out_5), .in_3(cs3_4_out_6), .in_4(cs3_4_out_7), .out_5(cs3_8_out_5),
    .out_6(cs3_8_out_6), .out_7(cs3_8_out_7), .out_8(cs3_8_out_8));
  CS3 cs3_9 (
    .in_1(cs3_4_out_8), .in_2(cs3_6_out_5), .in_3(cs3_6_out_6), .in_4(cs3_6_out_7), .out_5(cs3_9_out_5),
    .out_6(cs3_9_out_6), .out_7(cs3_9_out_7), .out_8(cs3_9_out_8));
  CS3 cs3_10 (
    .in_1(undriven[7]), .in_2(cs3_8_out_5), .in_3(cs3_8_out_6), .in_4(cs3_8_out_7), .out_5(cs3_10_out_5),
    .out_6(cs3_10_out_6), .out_7(cs3_10_out_7), .out_8(cs3_10_out_8));
  CS3 cs3_11 (
    .in_1(cs3_8_out_8), .in_2(cs3_9_out_5), .in_3(cs3_9_out_6), .in_4(cs3_9_out_7), .out_5(cs3_11_out_5),
    .out_6(cs3_11_out_6), .out_7(cs3_11_out_7), .out_8(cs3_11_out_8));
  CS3 cs3_12 (
    .in_1(cs3_9_out_8), .in_2(cs3_6_out_8), .in_3(cs3_7_out_8), .in_4(1'b0), .out_5(cs3_12_out_5),
    .out_6(cs3_12_out_6), .out_7(cs3_12_out_7), .out_8(cs3_12_out_8));
  CS3 cs3_13 (
    .in_1(undriven[6]), .in_2(cs3_10_out_5), .in_3(cs3_10_out_6), .in_4(cs3_10_out_7), .out_5(cs3_13_out_5),
    .out_6(cs3_13_out_6), .out_7(cs3_13_out_7), .out_8(cs3_13_out_8));
  CS3 cs3_14 (
    .in_1(cs3_10_out_8), .in_2(cs3_11_out_5), .in_3(cs3_11_out_6), .in_4(cs3_11_out_7), .out_5(cs3_14_out_5),
    .out_6(cs3_14_out_6), .out_7(cs3_14_out_7), .out_8(cs3_14_out_8));
  CS3 cs3_15 (
    .in_1(cs3_11_out_8), .in_2(cs3_12_out_5), .in_3(cs3_12_out_6), .in_4(cs3_12_out_7), .out_5(cs3_15_out_5),
    .out_6(cs3_15_out_6), .out_7(cs3_15_out_7), .out_8(cs3_15_out_8));
  CS3 cs3_16 (
    .in_1(undriven[5]), .in_2(cs3_13_out_5), .in_3(cs3_13_out_6), .in_4(cs3_13_out_7), .out_5(cs3_16_out_5),
    .out_6(cs3_16_out_6), .out_7(cs3_16_out_7), .out_8(cs3_16_out_8));
  CS3 cs3_17 (
    .in_1(cs3_13_out_8), .in_2(cs3_14_out_5), .in_3(cs3_14_out_6), .in_4(cs3_14_out_7), .out_5(cs3_17_out_5),
    .out_6(cs3_17_out_6), .out_7(cs3_17_out_7), .out_8(cs3_17_out_8));
  CS3 cs3_18 (
    .in_1(cs3_14_out_8), .in_2(cs3_15_out_5), .in_3(cs3_15_out_6), .in_4(cs3_15_out_7), .out_5(cs3_18_out_5),
    .out_6(cs3_18_out_6), .out_7(cs3_18_out_7), .out_8(cs3_18_out_8));
  CS3 cs3_19 (
    .in_1(undriven[4]), .in_2(cs3_16_out_5), .in_3(cs3_16_out_6), .in_4(cs3_16_out_7), .out_5(cs3_19_out_5),
    .out_6(cs3_19_out_6), .out_7(cs3_19_out_7), .out_8(cs3_19_out_8));
  CS3 cs3_20 (
    .in_1(cs3_16_out_8), .in_2(cs3_17_out_5), .in_3(cs3_17_out_6), .in_4(cs3_17_out_7), .out_5(cs3_20_out_5),
    .out_6(cs3_20_out_6), .out_7(cs3_20_out_7), .out_8(cs3_20_out_8));
  CS3 cs3_21 (
    .in_1(cs3_17_out_8), .in_2(cs3_18_out_5), .in_3(cs3_18_out_6), .in_4(cs3_18_out_7), .out_5(cs3_21_out_5),
    .out_6(cs3_21_out_6), .out_7(cs3_21_out_7), .out_8(cs3_21_out_8));
  CS3 cs3_22 (
    .in_1(cs3_18_out_8), .in_2(cs3_15_out_8), .in_3(cs3_12_out_8), .in_4(1'b0), .out_5(cs3_22_out_5),
    .out_6(cs3_22_out_6), .out_7(cs3_22_out_7), .out_8(cs3_22_out_8));
  CS3 cs3_23 (
    .in_1(undriven[3]), .in_2(cs3_19_out_5), .in_3(cs3_19_out_6), .in_4(cs3_19_out_7), .out_5(cs3_23_out_5),
    .out_6(cs3_23_out_6), .out_7(cs3_23_out_7), .out_8(cs3_23_out_8));
  CS3 cs3_24 (
    .in_1(cs3_19_out_8), .in_2(cs3_20_out_5), .in_3(cs3_20_out_6), .in_4(cs3_20_out_7), .out_5(cs3_24_out_5),
    .out_6(cs3_24_out_6), .out_7(cs3_24_out_7), .out_8(cs3_24_out_8));
  CS3 cs3_25 (
    .in_1(cs3_20_out_8), .in_2(cs3_21_out_5), .in_3(cs3_21_out_6), .in_4(cs3_21_out_7), .out_5(cs3_25_out_5),
    .out_6(cs3_25_out_6), .out_7(cs3_25_out_7), .out_8(cs3_25_out_8));
  CS3 cs3_26 (
    .in_1(cs3_21_out_8), .in_2(cs3_22_out_5), .in_3(cs3_22_out_6), .in_4(cs3_22_out_7), .out_5(cs3_26_out_5),
    .out_6(cs3_26_out_6), .out_7(cs3_26_out_7), .out_8(cs3_26_out_8));
  CS3 cs3_27 (
    .in_1(undriven[2]), .in_2(cs3_23_out_5), .in_3(cs3_23_out_6), .in_4(cs3_23_out_7), .out_5(cs3_27_out_5),
    .out_6(cs3_27_out_6), .out_7(cs3_27_out_7), .out_8(cs3_27_out_8));
  CS3 cs3_28 (
    .in_1(cs3_23_out_8), .in_2(cs3_24_out_5), .in_3(cs3_24_out_6), .in_4(cs3_24_out_7), .out_5(cs3_28_out_5),
    .out_6(cs3_28_out_6), .out_7(cs3_28_out_7), .out_8(cs3_28_out_8));
  CS3 cs3_29 (
    .in_1(cs3_24_out_8), .in_2(cs3_25_out_5), .in_3(cs3_25_out_6), .in_4(cs3_25_out_7), .out_5(cs3_29_out_5),
    .out_6(cs3_29_out_6), .out_7(cs3_29_out_7), .out_8(cs3_29_out_8));
  CS3 cs3_30 (
    .in_1(cs3_25_out_8), .in_2(cs3_26_out_5), .in_3(cs3_26_out_6), .in_4(cs3_26_out_7), .out_5(cs3_30_out_5),
    .out_6(cs3_30_out_6), .out_7(cs3_30_out_7), .out_8(cs3_30_out_8));
  CS3 cs3_31 (
    .in_1(undriven[1]), .in_2(cs3_27_out_5), .in_3(cs3_27_out_6), .in_4(cs3_27_out_7),
    .out_5(bcd_to_7_segment_decoder_5_p5[1]), .out_6(bcd_to_7_segment_decoder_5_p5[2]),
    .out_7(bcd_to_7_segment_decoder_5_p5[3]), .out_8(cs3_31_out_8[0]));
  CS3 cs3_32 (
    .in_1(cs3_27_out_8), .in_2(cs3_28_out_5), .in_3(cs3_28_out_6), .in_4(cs3_28_out_7),
    .out_5(cs3_31_out_8[1]), .out_6(cs3_31_out_8[2]), .out_7(cs3_31_out_8[3]), .out_8(cs3_32_out_8[0]));
  CS3 cs3_33 (
    .in_1(cs3_28_out_8), .in_2(cs3_29_out_5), .in_3(cs3_29_out_6), .in_4(cs3_29_out_7),
    .out_5(cs3_32_out_8[1]), .out_6(cs3_32_out_8[2]), .out_7(cs3_32_out_8[3]), .out_8(cs3_33_out_8[0]));
  CS3 cs3_34 (
    .in_1(cs3_29_out_8), .in_2(cs3_30_out_5), .in_3(cs3_30_out_6), .in_4(cs3_30_out_7),
    .out_5(cs3_33_out_8[1]), .out_6(cs3_33_out_8[2]), .out_7(cs3_33_out_8[3]), .out_8(cs3_34_out_8[0]));
  CS3 cs3_35 (
    .in_1(cs3_30_out_8), .in_2(cs3_26_out_8), .in_3(cs3_22_out_8), .in_4(1'b0), .out_5(cs3_34_out_8[1]),
    .out_6(cs3_34_out_8[2]), .out_7(cs3_34_out_8[3]), .out_8(cs3_35_out_8));
  // BCD_to_7_Segment_decoder bcd_to_7_segment_decoder_1: pin names not known; wires that end beside it: bcd_to_7_segment_decoder_1_p1, bcd_to_7_segment_decoder_1_p2, bcd_to_7_segment_decoder_1_p3, bcd_to_7_segment_decoder_1_p4, cs3_34_out_8, bcd_to_7_segment_decoder_1_p6, bcd_to_7_segment_decoder_1_p7, bcd_to_7_segment_decoder_1_p8
  _7_Segment_Display u_7_segment_display_1 (
    .g(bcd_to_7_segment_decoder_1_p1), .f(bcd_to_7_segment_decoder_1_p3), .a(bcd_to_7_segment_decoder_1_p6),
    .b(bcd_to_7_segment_decoder_1_p8), .e(bcd_to_7_segment_decoder_1_p2), .d(bcd_to_7_segment_decoder_1_p4),
    .c(bcd_to_7_segment_decoder_1_p7));  // open: dp
  // BCD_to_7_Segment_decoder bcd_to_7_segment_decoder_2: pin names not known; wires that end beside it: bcd_to_7_segment_decoder_2_p1, bcd_to_7_segment_decoder_2_p2, bcd_to_7_segment_decoder_2_p3, bcd_to_7_segment_decoder_2_p4, cs3_33_out_8, bcd_to_7_segment_decoder_2_p6, bcd_to_7_segment_decoder_2_p7, bcd_to_7_segment_decoder_2_p8
  _7_Segment_Display u_7_segment_display_2 (
    .g(bcd_to_7_segment_decoder_2_p1), .f(bcd_to_7_segment_decoder_2_p3), .a(bcd_to_7_segment_decoder_2_p6),
    .b(bcd_to_7_segment_decoder_2_p8), .e(bcd_to_7_segment_decoder_2_p2), .d(bcd_to_7_segment_decoder_2_p4),
    .c(bcd_to_7_segment_decoder_2_p7));  // open: dp
  // BCD_to_7_Segment_decoder bcd_to_7_segment_decoder_3: pin names not known; wires that end beside it: bcd_to_7_segment_decoder_3_p1, bcd_to_7_segment_decoder_3_p2, bcd_to_7_segment_decoder_3_p3, bcd_to_7_segment_decoder_3_p4, cs3_32_out_8, bcd_to_7_segment_decoder_3_p6, bcd_to_7_segment_decoder_3_p7, bcd_to_7_segment_decoder_3_p8
  _7_Segment_Display u_7_segment_display_3 (
    .g(bcd_to_7_segment_decoder_3_p1), .f(bcd_to_7_segment_decoder_3_p3), .a(bcd_to_7_segment_decoder_3_p6),
    .b(bcd_to_7_segment_decoder_3_p8), .e(bcd_to_7_segment_decoder_3_p2), .d(bcd_to_7_segment_decoder_3_p4),
    .c(bcd_to_7_segment_decoder_3_p7));  // open: dp
  // BCD_to_7_Segment_decoder bcd_to_7_segment_decoder_4: pin names not known; wires that end beside it: bcd_to_7_segment_decoder_4_p1, bcd_to_7_segment_decoder_4_p2, bcd_to_7_segment_decoder_4_p3, bcd_to_7_segment_decoder_4_p4, cs3_31_out_8, bcd_to_7_segment_decoder_4_p6, bcd_to_7_segment_decoder_4_p7, bcd_to_7_segment_decoder_4_p8
  _7_Segment_Display u_7_segment_display_4 (
    .g(bcd_to_7_segment_decoder_4_p1), .f(bcd_to_7_segment_decoder_4_p3), .a(bcd_to_7_segment_decoder_4_p6),
    .b(bcd_to_7_segment_decoder_4_p8), .e(bcd_to_7_segment_decoder_4_p2), .d(bcd_to_7_segment_decoder_4_p4),
    .c(bcd_to_7_segment_decoder_4_p7));  // open: dp
  // BCD_to_7_Segment_decoder bcd_to_7_segment_decoder_5: pin names not known; wires that end beside it: bcd_to_7_segment_decoder_5_p1, bcd_to_7_segment_decoder_5_p2, bcd_to_7_segment_decoder_5_p3, bcd_to_7_segment_decoder_5_p4, bcd_to_7_segment_decoder_5_p5, bcd_to_7_segment_decoder_5_p6, bcd_to_7_segment_decoder_5_p7, bcd_to_7_segment_decoder_5_p8
  _7_Segment_Display u_7_segment_display_5 (
    .g(bcd_to_7_segment_decoder_5_p1), .f(bcd_to_7_segment_decoder_5_p3), .a(bcd_to_7_segment_decoder_5_p6),
    .b(bcd_to_7_segment_decoder_5_p8), .e(bcd_to_7_segment_decoder_5_p2), .d(bcd_to_7_segment_decoder_5_p4),
    .c(bcd_to_7_segment_decoder_5_p7));  // open: dp
  // also tied to GND on the sheet: cs3_35_out_8
endmodule

module CS3 (
  input  in_1,
  input  in_2,
  input  in_3,
  input  in_4,
  output out_5,
  output out_6,
  output out_7,
  output out_8
);

  wire comparator_1_gt;
  wire [3:0] adder_1_out;

  Adder #(.width(4)) adder_1 (.a({in_4, in_3, in_2, in_1}), .b(4'b0011), .out(adder_1_out));  // open: cin, cout
  Comparator #(.mode("unsigned"), .width(4)) comparator_1 (
    .a({in_4, in_3, in_2, in_1}), .b(4'b0100), .gt(comparator_1_gt));  // open: eq, lt
  Multiplexer #(.width(4)) multiplexer_1 (
    .in0({in_4, in_3, in_2, in_1}), .in1(adder_1_out), .out({out_8, out_7, out_6, out_5}),
    .sel(comparator_1_gt));
endmodule
