// Logisim project signed seq multiplier.circ as structural Verilog: 8 circuits, main circuit MULTIPLICAND_REG_8BIT
module main (
  input  [7:0] MULTIPLICAND,
  input  [7:0] MULTIPLIER,
  output [7:0] out_3,
  output [7:0] out_4,
  output [15:0] PRODUCT
);

  wire CLK, mul_control_unit_1_alu_en, mul_control_unit_1_load_multpd, mul_control_unit_1_load_multpr,
       mul_control_unit_1_sel, mul_control_unit_1_shift, mul_control_unit_1_sn_multpd, P_IN, SN_R;

  Clock clock_1 (.out(CLK));
  MUL_CONTROL_UNIT mul_control_unit_1 (
    .CLK(CLK), .MULT_REG(out_3), .MULTIPLICAND(MULTIPLIER), .MULTIPLIER(MULTIPLICAND),
    .PROD_REG(PRODUCT[15:8]), .SN_MULTPD(mul_control_unit_1_sn_multpd), .SN_MULTPR(SN_R),
    .SEL(mul_control_unit_1_sel), .LOAD_MULTPD(mul_control_unit_1_load_multpd),
    .LOAD_MULTPR(mul_control_unit_1_load_multpr), .ALU_EN(mul_control_unit_1_alu_en),
    .SHIFT(mul_control_unit_1_shift));
  MULTIPLICAND_REG_8BIT multiplicand_reg_8bit_1 (
    .RST(1'b0), .LOAD(mul_control_unit_1_load_multpd), .SHIFT(mul_control_unit_1_shift), .CLK(CLK),
    .SN(SN_R), .MULTIPLICAND(MULTIPLICAND), .out_7(out_3));
  // ALU_8BIT alu_8bit_1: pin names not known; wires that end beside it: CLK, 1'b0, PRODUCT[15:8], out_4, out_3, mul_control_unit_1_alu_en
  PRODUCT_REG_17BIT product_reg_17bit_1 (
    .MULTIPLIER(MULTIPLIER), .ALU_IN(out_4), .LOAD_SEL(mul_control_unit_1_sel), .CLK(CLK),
    .LOAD(mul_control_unit_1_load_multpr), .SHIFT(mul_control_unit_1_shift),
    .SN(mul_control_unit_1_sn_multpd), .MULH(PRODUCT[15:8]), .MUL(PRODUCT[7:0]), .Q_16(P_IN));  // open: RST

  // Other names for the same wires on the sheet: MLT_R[7:0] = out_3
endmodule

module ALU_8BIT (
  input  EN,
  input  CIN,
  input  [7:0] A,
  input  [7:0] B,
  output [7:0] RESULT,
  output COUT
);

  wire [7:0] adder_1_out;

  Adder adder_1 (.a(A), .b(B), .out(adder_1_out), .cin(CIN), .cout(COUT));
  Multiplexer #(.width(8)) multiplexer_1 (.in0({8{1'b0}}), .in1(adder_1_out), .out(RESULT), .sel(EN));
endmodule

module MULTIPLICAND_REG_8BIT (
  input  RST,
  input  LOAD,
  input  SHIFT,
  input  CLK,
  input  SN,
  input  [7:0] MULTIPLICAND,
  output [7:0] out_7
);

  // Shift_Register shift_register_1: pin names not known; wires that end beside it: RST, LOAD, SHIFT, CLK, SN, MULTIPLICAND[0], MULTIPLICAND[1], MULTIPLICAND[2], MULTIPLICAND[3], MULTIPLICAND[4], MULTIPLICAND[5], MULTIPLICAND[6], MULTIPLICAND[7], out_7[0], out_7[1], out_7[2], out_7[3], out_7[4], out_7[5], out_7[6], out_7[7]
endmodule

module MUL_CONTROL_UNIT (
  input  [7:0] MULT_REG,
  input  [7:0] MULTIPLICAND,
  input  [7:0] MULTIPLIER,
  input  CLK,
  input  [7:0] PROD_REG,
  output SHIFT,
  output SEL,
  output LOAD_MULTPD,
  output LOAD_MULTPR,
  output ALU_EN,
  output SN_MULTPD,
  output SN_MULTPR
);

  wire or_1_out, or_2_out, or_3_out;
  wire [7:0] register_1_q, register_2_q, xor_1_out, xor_2_out;

  Register register_1 (.D(MULTIPLICAND), .clk(CLK), .Q(register_1_q), .clr(1'b0));  // open: en
  Register register_2 (.D(MULTIPLIER), .clk(CLK), .Q(register_2_q), .clr(1'b0));  // open: en
  assign xor_1_out = register_1_q ^ MULTIPLICAND;  // XOR_Gate xor_1, 8 bits wide
  assign xor_2_out = register_2_q ^ MULTIPLIER;  // XOR_Gate xor_2, 8 bits wide
  or or_1 (or_1_out, MULT_REG[0], MULT_REG[1], MULT_REG[2], MULT_REG[3], MULT_REG[4], MULT_REG[5], MULT_REG[6], MULT_REG[7]);
  or or_2 (or_2_out, xor_1_out[0], xor_1_out[1], xor_1_out[2], xor_1_out[3], xor_1_out[4], xor_1_out[5], xor_1_out[6], xor_1_out[7]);
  or or_3 (or_3_out, xor_2_out[0], xor_2_out[1], xor_2_out[2], xor_2_out[3], xor_2_out[4], xor_2_out[5], xor_2_out[6], xor_2_out[7]);
  or or_4 (LOAD_MULTPD, or_2_out, or_3_out);
  not not_1 (SEL, LOAD_MULTPD);
  or or_5 (LOAD_MULTPR, PROD_REG[0], LOAD_MULTPD);
  and and_1 (SHIFT, or_1_out, ~LOAD_MULTPD);  // AND_Gate

  assign ALU_EN = PROD_REG[0];
  assign SN_MULTPD = MULTIPLICAND[7];
  assign SN_MULTPR = MULTIPLIER[7];

  // Notes on the sheet:
  //   ~END OF MULT
  //   NEW INPUT
  //   CHANGE
endmodule

module PRODUCT_REG_17BIT (
  input  [7:0] MULTIPLIER,
  input  [7:0] ALU_IN,
  input  LOAD_SEL,
  input  CLK,
  input  RST,
  input  LOAD,
  input  SHIFT,
  input  SN,
  output [7:0] MULH,
  output [7:0] MUL,
  output Q_16
);

  wire [7:0] multiplexer_1_out;

  Multiplexer #(.width(8)) multiplexer_1 (.in0(MULTIPLIER), .in1(ALU_IN), .out(multiplexer_1_out), .sel(LOAD_SEL));
  D_Flip_Flop d_ff_1 (.D(SN), .clk(CLK), .Q(Q_16), .reset(RST));  // open: Qn, preset
  SRR_REG_16BIT srr_reg_16bit_1 (
    .I_0(MUL[0]), .I_1(MUL[1]), .I_2(MUL[2]), .I_3(MUL[3]), .I_4(MUL[4]), .I_5(MUL[5]), .I_6(MUL[6]),
    .I_7(MUL[7]), .I_8(multiplexer_1_out[0]), .I_9(multiplexer_1_out[1]), .I_10(multiplexer_1_out[2]),
    .I_11(multiplexer_1_out[3]), .I_12(multiplexer_1_out[4]), .I_13(multiplexer_1_out[5]),
    .I_14(multiplexer_1_out[6]), .I_15(multiplexer_1_out[7]), .END_D(Q_16), .END_I(1'b0), .CLK(CLK),
    .RST(RST), .LOAD(LOAD), .SHIFT(SHIFT), .Q_0(MUL[0]), .Q_1(MUL[1]), .Q_2(MUL[2]), .Q_3(MUL[3]),
    .Q_4(MUL[4]), .Q_5(MUL[5]), .Q_6(MUL[6]), .Q_7(MUL[7]), .Q_8(MULH[0]), .Q_9(MULH[1]), .Q_10(MULH[2]),
    .Q_11(MULH[3]), .Q_12(MULH[4]), .Q_13(MULH[5]), .Q_14(MULH[6]), .Q_15(MULH[7]));

  // Other names for the same wires on the sheet: SH_LD[1:0] = {LOAD, SHIFT}
endmodule

module SRR_REG_4BIT (
  input  I_0,
  input  I_1,
  input  I_2,
  input  I_4,
  input  END_D,
  input  END_I,
  input  CLK,
  input  RST,
  input  LOAD,
  input  SHIFT,
  output Q_0,
  output Q_1,
  output Q_2,
  output Q_3
);

  wire multiplexer_1_out, multiplexer_2_out, multiplexer_3_out, multiplexer_4_out;

  Multiplexer #(.select(2)) multiplexer_1 (
    .in1(Q_1), .in2(I_0), .in3(I_1), .out(multiplexer_1_out), .sel({LOAD, SHIFT}));  // open: in0
  D_Flip_Flop d_ff_1 (.D(multiplexer_1_out), .clk(CLK), .Q(Q_0), .reset(RST));  // open: Qn, preset
  D_Flip_Flop d_ff_2 (.D(multiplexer_2_out), .clk(CLK), .Q(Q_1), .reset(RST));  // open: Qn, preset
  Multiplexer #(.select(2)) multiplexer_2 (
    .in1(Q_2), .in2(I_1), .in3(I_2), .out(multiplexer_2_out), .sel({LOAD, SHIFT}));  // open: in0
  D_Flip_Flop d_ff_3 (.D(multiplexer_3_out), .clk(CLK), .Q(Q_2), .reset(RST));  // open: Qn, preset
  Multiplexer #(.select(2)) multiplexer_3 (
    .in1(Q_3), .in2(I_2), .in3(I_4), .out(multiplexer_3_out), .sel({LOAD, SHIFT}));  // open: in0
  D_Flip_Flop d_ff_4 (.D(multiplexer_4_out), .clk(CLK), .Q(Q_3), .reset(RST));  // open: Qn, preset
  Multiplexer #(.select(2)) multiplexer_4 (
    .in1(END_D), .in2(I_4), .in3(END_I), .out(multiplexer_4_out), .sel({LOAD, SHIFT}));  // open: in0

  // Other names for the same wires on the sheet: SH_LD[1:0] = {LOAD, SHIFT}
endmodule

module SRR_REG_16BIT (
  input  I_0,
  input  I_1,
  input  I_2,
  input  I_3,
  input  I_4,
  input  I_5,
  input  I_6,
  input  I_7,
  input  I_8,
  input  I_9,
  input  I_10,
  input  I_11,
  input  I_12,
  input  I_13,
  input  I_14,
  input  I_15,
  input  END_D,
  input  END_I,
  input  CLK,
  input  RST,
  input  LOAD,
  input  SHIFT,
  output Q_0,
  output Q_1,
  output Q_2,
  output Q_3,
  output Q_4,
  output Q_5,
  output Q_6,
  output Q_7,
  output Q_8,
  output Q_9,
  output Q_10,
  output Q_11,
  output Q_12,
  output Q_13,
  output Q_14,
  output Q_15
);

  SRR_REG_4BIT srr_reg_4bit_1 (
    .I_0(I_0), .I_1(I_1), .I_2(I_2), .I_4(I_3), .END_D(Q_4), .END_I(I_4), .CLK(CLK), .RST(RST), .LOAD(LOAD),
    .SHIFT(SHIFT), .Q_0(Q_0), .Q_1(Q_1), .Q_2(Q_2), .Q_3(Q_3));
  SRR_REG_4BIT srr_reg_4bit_2 (
    .I_0(I_8), .I_1(I_9), .I_2(I_10), .I_4(I_11), .END_D(Q_12), .END_I(I_12), .CLK(CLK), .RST(RST),
    .LOAD(LOAD), .SHIFT(SHIFT), .Q_0(Q_8), .Q_1(Q_9), .Q_2(Q_10), .Q_3(Q_11));
  SRR_REG_4BIT srr_reg_4bit_3 (
    .I_0(I_4), .I_1(I_5), .I_2(I_6), .I_4(I_7), .END_D(Q_8), .END_I(I_8), .CLK(CLK), .RST(RST), .LOAD(LOAD),
    .SHIFT(SHIFT), .Q_0(Q_4), .Q_1(Q_5), .Q_2(Q_6), .Q_3(Q_7));
  SRR_REG_4BIT srr_reg_4bit_4 (
    .I_0(I_12), .I_1(I_13), .I_2(I_14), .I_4(I_15), .END_D(END_D), .END_I(END_I), .CLK(CLK), .RST(RST),
    .LOAD(LOAD), .SHIFT(SHIFT), .Q_0(Q_12), .Q_1(Q_13), .Q_2(Q_14), .Q_3(Q_15));
endmodule

module SS_MUL (
  input  [7:0] MULTIPLICAND,
  input  [7:0] MULTIPLIER,
  output [15:0] PRODUCT
);

  wire CLK, mul_control_unit_1_alu_en, mul_control_unit_1_load_multpd, mul_control_unit_1_load_multpr,
       mul_control_unit_1_sel, mul_control_unit_1_shift, mul_control_unit_1_sn_multpd,
       mul_control_unit_1_sn_multpr;
  wire [7:0] alu_8bit_1_p4, multiplicand_reg_8bit_1_out_7;

  Clock clock_1 (.out(CLK));
  MULTIPLICAND_REG_8BIT multiplicand_reg_8bit_1 (
    .RST(mul_control_unit_1_sn_multpd), .LOAD(mul_control_unit_1_load_multpd),
    .SHIFT(mul_control_unit_1_shift), .CLK(CLK), .SN(mul_control_unit_1_sn_multpd),
    .MULTIPLICAND(MULTIPLICAND), .out_7(multiplicand_reg_8bit_1_out_7));
  MUL_CONTROL_UNIT mul_control_unit_1 (
    .CLK(CLK), .MULT_REG(multiplicand_reg_8bit_1_out_7), .MULTIPLICAND(MULTIPLICAND),
    .MULTIPLIER(MULTIPLIER), .PROD_REG(PRODUCT[7:0]), .SN_MULTPD(mul_control_unit_1_sn_multpd),
    .SN_MULTPR(mul_control_unit_1_sn_multpr), .SEL(mul_control_unit_1_sel),
    .LOAD_MULTPD(mul_control_unit_1_load_multpd), .LOAD_MULTPR(mul_control_unit_1_load_multpr),
    .ALU_EN(mul_control_unit_1_alu_en), .SHIFT(mul_control_unit_1_shift));
  PRODUCT_REG_17BIT product_reg_17bit_1 (
    .MULTIPLIER(MULTIPLIER), .ALU_IN(alu_8bit_1_p4), .LOAD_SEL(mul_control_unit_1_sel), .CLK(CLK),
    .RST(mul_control_unit_1_sn_multpr), .LOAD(mul_control_unit_1_load_multpr),
    .SHIFT(mul_control_unit_1_shift), .SN(mul_control_unit_1_sn_multpr), .MULH(PRODUCT[15:8]),
    .MUL(PRODUCT[7:0]));  // open: Q_16
  // ALU_8BIT alu_8bit_1: pin names not known; wires that end beside it: CLK, mul_control_unit_1_sn_multpd, multiplicand_reg_8bit_1_out_7, alu_8bit_1_p4, PRODUCT[7:0], mul_control_unit_1_alu_en
endmodule
