// Logisim project unsigned_mulitiplier.circ as structural Verilog: 5 circuits, main circuit PROD_REG
module MAIN2 (
  input  in_1,
  input  SIGN,
  input  [7:0] MULTIPLIER,
  input  [7:0] MULTIPLICAND,
  input  [15:0] zero,
  output [7:0] out_6,
  output [7:0] out_7,
  output [16:0] PROD_DEC,
  output [16:0] PROD_BIN
);

  wire adder_1_cout, and_1_out, and_2_out, bcd_to_7_segment_decoder_1_p1, bcd_to_7_segment_decoder_1_p2,
       bcd_to_7_segment_decoder_1_p3, bcd_to_7_segment_decoder_1_p4, bcd_to_7_segment_decoder_1_p6,
       bcd_to_7_segment_decoder_1_p7, bcd_to_7_segment_decoder_1_p8, bcd_to_7_segment_decoder_2_p1,
       bcd_to_7_segment_decoder_2_p2, bcd_to_7_segment_decoder_2_p3, bcd_to_7_segment_decoder_2_p4,
       bcd_to_7_segment_decoder_2_p6, bcd_to_7_segment_decoder_2_p7, bcd_to_7_segment_decoder_2_p8,
       bcd_to_7_segment_decoder_3_p1, bcd_to_7_segment_decoder_3_p2, bcd_to_7_segment_decoder_3_p3,
       bcd_to_7_segment_decoder_3_p4, bcd_to_7_segment_decoder_3_p6, bcd_to_7_segment_decoder_3_p7,
       bcd_to_7_segment_decoder_3_p8, bcd_to_7_segment_decoder_4_p1, bcd_to_7_segment_decoder_4_p2,
       bcd_to_7_segment_decoder_4_p3, bcd_to_7_segment_decoder_4_p4, bcd_to_7_segment_decoder_4_p6,
       bcd_to_7_segment_decoder_4_p7, bcd_to_7_segment_decoder_4_p8, bcd_to_7_segment_decoder_5_p1,
       bcd_to_7_segment_decoder_5_p2, bcd_to_7_segment_decoder_5_p3, bcd_to_7_segment_decoder_5_p4,
       bcd_to_7_segment_decoder_5_p6, bcd_to_7_segment_decoder_5_p7, bcd_to_7_segment_decoder_5_p8,
       button_1_out, CLK_out, cu_1_end_count, cu_1_load_en, cu_1_mux_sel, cu_1_zero_flag, not_1_out,
       not_2_out, or_1_out, t_ff_1_q;
  wire [3:0] bcd_7seg_1_first, bcd_7seg_1_fourth, bcd_7seg_1_second, bcd_7seg_1_third,
       bcd_to_7_segment_decoder_1_p5;
  wire [7:0] adder_1_out, multiplexer_1_out;
  wire [15:0] multiplexer_2_out;

  Button button_1 (.out(button_1_out));
  Multiplexer #(.width(8)) multiplexer_1 (
    .in0({8{1'b0}}), .in1(MULTIPLICAND), .out(multiplexer_1_out), .sel(cu_1_mux_sel));
  Clock CLK (.out(CLK_out));
  Adder adder_1 (.a(out_6), .b(multiplexer_1_out), .out(adder_1_out), .cout(adder_1_cout));  // open: cin
  T_Flip_Flop t_ff_1 (.T(in_1), .clk(or_1_out), .Q(t_ff_1_q));  // open: Qn, reset, preset
  or or_1 (or_1_out, button_1_out, cu_1_zero_flag, cu_1_end_count);
  not not_1 (not_1_out, cu_1_load_en);
  not not_2 (not_2_out, t_ff_1_q);
  and and_1 (and_1_out, t_ff_1_q, cu_1_load_en);
  and and_2 (and_2_out, t_ff_1_q, not_1_out);
  LED led_1 (.in(not_2_out));
  PROD_REG prod_reg_1 (
    .rst(button_1_out), .load(and_1_out), .shift(and_2_out), .clk(CLK_out), .sn(SIGN), .alu_in(adder_1_out),
    .cout(adder_1_cout), .multiplier(MULTIPLIER), .sel(cu_1_mux_sel), .prod(PROD_BIN), .UPPER_HALF(out_6),
    .LOWER_HALF(out_7));
  CU cu_1 (
    .rst_crc(button_1_out), .clk(CLK_out), .shift_en(and_2_out), .b0(out_7[0]), .multiplier(MULTIPLIER),
    .End_count(cu_1_end_count), .load_en(cu_1_load_en), .mux_sel(cu_1_mux_sel), .zero_flag(cu_1_zero_flag));
  Multiplexer #(.width(16)) multiplexer_2 (
    .in0(zero), .in1(PROD_BIN[15:0]), .out(multiplexer_2_out), .sel(cu_1_end_count));
  // BCD_to_7_Segment_decoder bcd_to_7_segment_decoder_1: pin names not known; wires that end beside it: bcd_to_7_segment_decoder_1_p1, bcd_to_7_segment_decoder_1_p2, bcd_to_7_segment_decoder_1_p3, bcd_to_7_segment_decoder_1_p4, bcd_to_7_segment_decoder_1_p5, bcd_to_7_segment_decoder_1_p6, bcd_to_7_segment_decoder_1_p7, bcd_to_7_segment_decoder_1_p8
  _7_Segment_Display u_7_segment_display_1 (
    .g(bcd_to_7_segment_decoder_1_p1), .f(bcd_to_7_segment_decoder_1_p3), .a(bcd_to_7_segment_decoder_1_p6),
    .b(bcd_to_7_segment_decoder_1_p8), .e(bcd_to_7_segment_decoder_1_p2), .d(bcd_to_7_segment_decoder_1_p4),
    .c(bcd_to_7_segment_decoder_1_p7));  // open: dp
  BCD_7SEG bcd_7seg_1 (
    .PROD_16(multiplexer_2_out), .FIFTH(bcd_to_7_segment_decoder_1_p5), .FOURTH(bcd_7seg_1_fourth),
    .THIRD(bcd_7seg_1_third), .SECOND(bcd_7seg_1_second), .FIRST(bcd_7seg_1_first));
  // BCD_to_7_Segment_decoder bcd_to_7_segment_decoder_2: pin names not known; wires that end beside it: bcd_to_7_segment_decoder_2_p1, bcd_to_7_segment_decoder_2_p2, bcd_to_7_segment_decoder_2_p3, bcd_to_7_segment_decoder_2_p4, bcd_7seg_1_fourth, bcd_to_7_segment_decoder_2_p6, bcd_to_7_segment_decoder_2_p7, bcd_to_7_segment_decoder_2_p8
  _7_Segment_Display u_7_segment_display_2 (
    .g(bcd_to_7_segment_decoder_2_p1), .f(bcd_to_7_segment_decoder_2_p3), .a(bcd_to_7_segment_decoder_2_p6),
    .b(bcd_to_7_segment_decoder_2_p8), .e(bcd_to_7_segment_decoder_2_p2), .d(bcd_to_7_segment_decoder_2_p4),
    .c(bcd_to_7_segment_decoder_2_p7));  // open: dp
  // BCD_to_7_Segment_decoder bcd_to_7_segment_decoder_3: pin names not known; wires that end beside it: bcd_to_7_segment_decoder_3_p1, bcd_to_7_segment_decoder_3_p2, bcd_to_7_segment_decoder_3_p3, bcd_to_7_segment_decoder_3_p4, bcd_7seg_1_third, bcd_to_7_segment_decoder_3_p6, bcd_to_7_segment_decoder_3_p7, bcd_to_7_segment_decoder_3_p8
  _7_Segment_Display u_7_segment_display_3 (
    .g(bcd_to_7_segment_decoder_3_p1), .f(bcd_to_7_segment_decoder_3_p3), .a(bcd_to_7_segment_decoder_3_p6),
    .b(bcd_to_7_segment_decoder_3_p8), .e(bcd_to_7_segment_decoder_3_p2), .d(bcd_to_7_segment_decoder_3_p4),
    .c(bcd_to_7_segment_decoder_3_p7));  // open: dp
  // BCD_to_7_Segment_decoder bcd_to_7_segment_decoder_4: pin names not known; wires that end beside it: bcd_to_7_segment_decoder_4_p1, bcd_to_7_segment_decoder_4_p2, bcd_to_7_segment_decoder_4_p3, bcd_to_7_segment_decoder_4_p4, bcd_7seg_1_second, bcd_to_7_segment_decoder_4_p6, bcd_to_7_segment_decoder_4_p7, bcd_to_7_segment_decoder_4_p8
  _7_Segment_Display u_7_segment_display_4 (
    .g(bcd_to_7_segment_decoder_4_p1), .f(bcd_to_7_segment_decoder_4_p3), .a(bcd_to_7_segment_decoder_4_p6),
    .b(bcd_to_7_segment_decoder_4_p8), .e(bcd_to_7_segment_decoder_4_p2), .d(bcd_to_7_segment_decoder_4_p4),
    .c(bcd_to_7_segment_decoder_4_p7));  // open: dp
  // BCD_to_7_Segment_decoder bcd_to_7_segment_decoder_5: pin names not known; wires that end beside it: bcd_to_7_segment_decoder_5_p1, bcd_to_7_segment_decoder_5_p2, bcd_to_7_segment_decoder_5_p3, bcd_to_7_segment_decoder_5_p4, bcd_7seg_1_first, bcd_to_7_segment_decoder_5_p6, bcd_to_7_segment_decoder_5_p7, bcd_to_7_segment_decoder_5_p8
  _7_Segment_Display u_7_segment_display_5 (
    .g(bcd_to_7_segment_decoder_5_p1), .f(bcd_to_7_segment_decoder_5_p3), .a(bcd_to_7_segment_decoder_5_p6),
    .b(bcd_to_7_segment_decoder_5_p8), .e(bcd_to_7_segment_decoder_5_p2), .d(bcd_to_7_segment_decoder_5_p4),
    .c(bcd_to_7_segment_decoder_5_p7));  // open: dp

  assign PROD_DEC = PROD_BIN;
endmodule

module PROD_REG (
  input  rst,
  input  load,
  input  shift,
  input  clk,
  input  sn,
  input  [7:0] alu_in,
  input  cout,
  input  [7:0] multiplier,
  input  sel,
  output [16:0] prod,
  output [7:0] UPPER_HALF,
  output [7:0] LOWER_HALF
);

  wire [7:0] multiplexer_1_out;

  Multiplexer #(.width(8)) multiplexer_1 (.in0(multiplier), .in1(LOWER_HALF), .out(multiplexer_1_out), .sel(sel));
  // Shift_Register #(.length(17)) shift_register_1: pin names not known; wires that end beside it: rst, load, shift, clk, sn, cout, alu_in[7], alu_in[6], alu_in[5], alu_in[4], alu_in[3], alu_in[2], alu_in[1], alu_in[0], multiplexer_1_out[7], multiplexer_1_out[6], multiplexer_1_out[5], prod[16], prod[15], prod[14], prod[13], prod[12], prod[11], prod[10], prod[9], prod[8], LOWER_HALF[7], LOWER_HALF[6], LOWER_HALF[5]

  assign prod[7:0] = LOWER_HALF;
  assign UPPER_HALF = prod[15:8];
endmodule

module BCD_SUBMODULE (
  input  in_1,
  input  in_2,
  input  in_3,
  input  in_4,
  output out_5,
  output out_6,
  output out_7,
  output out_8
);

  wire comparator_1_gt;
  wire [3:0] adder_1_out;

  Adder #(.width(4)) adder_1 (.a({in_4, in_3, in_2, in_1}), .b(4'b0011), .out(adder_1_out));  // open: cin, cout
  Comparator #(.mode("unsigned"), .width(4)) comparator_1 (
    .a({in_4, in_3, in_2, in_1}), .b(4'b0100), .gt(comparator_1_gt));  // open: eq, lt
  Multiplexer #(.width(4)) multiplexer_1 (
    .in0({in_4, in_3, in_2, in_1}), .in1(adder_1_out), .out({out_8, out_7, out_6, out_5}),
    .sel(comparator_1_gt));
endmodule

module BCD_7SEG (
  input  [15:0] PROD_16,
  output [3:0] FIFTH,
  output [3:0] FOURTH,
  output [3:0] THIRD,
  output [3:0] SECOND,
  output [3:0] FIRST
);

  wire bcd_submodule_1_out_5, bcd_submodule_1_out_6, bcd_submodule_1_out_7, bcd_submodule_1_out_8,
       bcd_submodule_2_out_5, bcd_submodule_2_out_6, bcd_submodule_2_out_7, bcd_submodule_2_out_8,
       bcd_submodule_3_out_5, bcd_submodule_3_out_6, bcd_submodule_3_out_7, bcd_submodule_3_out_8,
       bcd_submodule_4_out_5, bcd_submodule_4_out_6, bcd_submodule_4_out_7, bcd_submodule_4_out_8,
       bcd_submodule_5_out_5, bcd_submodule_5_out_6, bcd_submodule_5_out_7, bcd_submodule_5_out_8,
       bcd_submodule_6_out_5, bcd_submodule_6_out_6, bcd_submodule_6_out_7, bcd_submodule_6_out_8,
       bcd_submodule_7_out_5, bcd_submodule_7_out_6, bcd_submodule_7_out_7, bcd_submodule_7_out_8,
       bcd_submodule_8_out_5, bcd_submodule_8_out_6, bcd_submodule_8_out_7, bcd_submodule_8_out_8,
       bcd_submodule_9_out_5, bcd_submodule_9_out_6, bcd_submodule_9_out_7, bcd_submodule_9_out_8,
       bcd_submodule_10_out_5, bcd_submodule_10_out_6, bcd_submodule_10_out_7, bcd_submodule_10_out_8,
       bcd_submodule_11_out_5, bcd_submodule_11_out_6, bcd_submodule_11_out_7, bcd_submodule_11_out_8,
       bcd_submodule_12_out_5, bcd_submodule_12_out_6, bcd_submodule_12_out_7, bcd_submodule_12_out_8,
       bcd_submodule_13_out_5, bcd_submodule_13_out_6, bcd_submodule_13_out_7, bcd_submodule_13_out_8,
       bcd_submodule_14_out_5, bcd_submodule_14_out_6, bcd_submodule_14_out_7, bcd_submodule_14_out_8,
       bcd_submodule_15_out_5, bcd_submodule_15_out_6, bcd_submodule_15_out_7, bcd_submodule_15_out_8,
       bcd_submodule_16_out_5, bcd_submodule_16_out_6, bcd_submodule_16_out_7, bcd_submodule_16_out_8,
       bcd_submodule_17_out_5, bcd_submodule_17_out_6, bcd_submodule_17_out_7, bcd_submodule_17_out_8,
       bcd_submodule_18_out_5, bcd_submodule_18_out_6, bcd_submodule_18_out_7, bcd_submodule_18_out_8,
       bcd_submodule_19_out_5, bcd_submodule_19_out_6, bcd_submodule_19_out_7, bcd_submodule_19_out_8,
       bcd_submodule_20_out_5, bcd_submodule_20_out_6, bcd_submodule_20_out_7, bcd_submodule_20_out_8,
       bcd_submodule_21_out_5, bcd_submodule_21_out_6, bcd_submodule_21_out_7, bcd_submodule_21_out_8,
       bcd_submodule_22_out_5, bcd_submodule_22_out_6, bcd_submodule_22_out_7, bcd_submodule_22_out_8,
       bcd_submodule_23_out_5, bcd_submodule_23_out_6, bcd_submodule_23_out_7, bcd_submodule_23_out_8,
       bcd_submodule_24_out_5, bcd_submodule_24_out_6, bcd_submodule_24_out_7, bcd_submodule_24_out_8,
       bcd_submodule_25_out_5, bcd_submodule_25_out_6, bcd_submodule_25_out_7, bcd_submodule_25_out_8,
       bcd_submodule_26_out_5, bcd_submodule_26_out_6, bcd_submodule_26_out_7, bcd_submodule_26_out_8,
       bcd_submodule_27_out_5, bcd_submodule_27_out_6, bcd_submodule_27_out_7, bcd_submodule_27_out_8,
       bcd_submodule_28_out_5, bcd_submodule_28_out_6, bcd_submodule_28_out_7, bcd_submodule_28_out_8,
       bcd_submodule_29_out_5, bcd_submodule_29_out_6, bcd_submodule_29_out_7, bcd_submodule_29_out_8,
       bcd_submodule_30_out_5, bcd_submodule_30_out_6, bcd_submodule_30_out_7, bcd_submodule_30_out_8,
       bcd_submodule_32_out_8;

  BCD_SUBMODULE bcd_submodule_1 (
    .in_1(PROD_16[13]), .in_2(PROD_16[14]), .in_3(PROD_16[15]), .in_4(1'b0), .out_5(bcd_submodule_1_out_5),
    .out_6(bcd_submodule_1_out_6), .out_7(bcd_submodule_1_out_7), .out_8(bcd_submodule_1_out_8));
  BCD_SUBMODULE bcd_submodule_2 (
    .in_1(PROD_16[12]), .in_2(bcd_submodule_1_out_5), .in_3(bcd_submodule_1_out_6),
    .in_4(bcd_submodule_1_out_7), .out_5(bcd_submodule_2_out_5), .out_6(bcd_submodule_2_out_6),
    .out_7(bcd_submodule_2_out_7), .out_8(bcd_submodule_2_out_8));
  BCD_SUBMODULE bcd_submodule_3 (
    .in_1(PROD_16[11]), .in_2(bcd_submodule_2_out_5), .in_3(bcd_submodule_2_out_6),
    .in_4(bcd_submodule_2_out_7), .out_5(bcd_submodule_3_out_5), .out_6(bcd_submodule_3_out_6),
    .out_7(bcd_submodule_3_out_7), .out_8(bcd_submodule_3_out_8));
  BCD_SUBMODULE bcd_submodule_4 (
    .in_1(PROD_16[10]), .in_2(bcd_submodule_3_out_5), .in_3(bcd_submodule_3_out_6),
    .in_4(bcd_submodule_3_out_7), .out_5(bcd_submodule_4_out_5), .out_6(bcd_submodule_4_out_6),
    .out_7(bcd_submodule_4_out_7), .out_8(bcd_submodule_4_out_8));
  BCD_SUBMODULE bcd_submodule_5 (
    .in_1(bcd_submodule_3_out_8), .in_2(bcd_submodule_2_out_8), .in_3(bcd_submodule_1_out_8), .in_4(1'b0),
    .out_5(bcd_submodule_5_out_5), .out_6(bcd_submodule_5_out_6), .out_7(bcd_submodule_5_out_7),
    .out_8(bcd_submodule_5_out_8));
  BCD_SUBMODULE bcd_submodule_6 (
    .in_1(PROD_16[9]), .in_2(bcd_submodule_4_out_5), .in_3(bcd_submodule_4_out_6),
    .in_4(bcd_submodule_4_out_7), .out_5(bcd_submodule_6_out_5), .out_6(bcd_submodule_6_out_6),
    .out_7(bcd_submodule_6_out_7), .out_8(bcd_submodule_6_out_8));
  BCD_SUBMODULE bcd_submodule_7 (
    .in_1(bcd_submodule_4_out_8), .in_2(bcd_submodule_5_out_5), .in_3(bcd_submodule_5_out_6),
    .in_4(bcd_submodule_5_out_7), .out_5(bcd_submodule_7_out_5), .out_6(bcd_submodule_7_out_6),
    .out_7(bcd_submodule_7_out_7), .out_8(bcd_submodule_7_out_8));
  BCD_SUBMODULE bcd_submodule_8 (
    .in_1(PROD_16[8]), .in_2(bcd_submodule_6_out_5), .in_3(bcd_submodule_6_out_6),
    .in_4(bcd_submodule_6_out_7), .out_5(bcd_submodule_8_out_5), .out_6(bcd_submodule_8_out_6),
    .out_7(bcd_submodule_8_out_7), .out_8(bcd_submodule_8_out_8));
  BCD_SUBMODULE bcd_submodule_9 (
    .in_1(bcd_submodule_6_out_8), .in_2(bcd_submodule_7_out_5), .in_3(bcd_submodule_7_out_6),
    .in_4(bcd_submodule_7_out_7), .out_5(bcd_submodule_9_out_5), .out_6(bcd_submodule_9_out_6),
    .out_7(bcd_submodule_9_out_7), .out_8(bcd_submodule_9_out_8));
  BCD_SUBMODULE bcd_submodule_10 (
    .in_1(PROD_16[6]), .in_2(bcd_submodule_11_out_5), .in_3(bcd_submodule_11_out_6),
    .in_4(bcd_submodule_11_out_7), .out_5(bcd_submodule_10_out_5), .out_6(bcd_submodule_10_out_6),
    .out_7(bcd_submodule_10_out_7), .out_8(bcd_submodule_10_out_8));
  BCD_SUBMODULE bcd_submodule_11 (
    .in_1(PROD_16[7]), .in_2(bcd_submodule_8_out_5), .in_3(bcd_submodule_8_out_6),
    .in_4(bcd_submodule_8_out_7), .out_5(bcd_submodule_11_out_5), .out_6(bcd_submodule_11_out_6),
    .out_7(bcd_submodule_11_out_7), .out_8(bcd_submodule_11_out_8));
  BCD_SUBMODULE bcd_submodule_12 (
    .in_1(bcd_submodule_11_out_8), .in_2(bcd_submodule_13_out_5), .in_3(bcd_submodule_13_out_6),
    .in_4(bcd_submodule_13_out_7), .out_5(bcd_submodule_12_out_5), .out_6(bcd_submodule_12_out_6),
    .out_7(bcd_submodule_12_out_7), .out_8(bcd_submodule_12_out_8));
  BCD_SUBMODULE bcd_submodule_13 (
    .in_1(bcd_submodule_8_out_8), .in_2(bcd_submodule_9_out_5), .in_3(bcd_submodule_9_out_6),
    .in_4(bcd_submodule_9_out_7), .out_5(bcd_submodule_13_out_5), .out_6(bcd_submodule_13_out_6),
    .out_7(bcd_submodule_13_out_7), .out_8(bcd_submodule_13_out_8));
  BCD_SUBMODULE bcd_submodule_14 (
    .in_1(bcd_submodule_13_out_8), .in_2(bcd_submodule_15_out_5), .in_3(bcd_submodule_15_out_6),
    .in_4(bcd_submodule_15_out_7), .out_5(bcd_submodule_14_out_5), .out_6(bcd_submodule_14_out_6),
    .out_7(bcd_submodule_14_out_7), .out_8(bcd_submodule_14_out_8));
  BCD_SUBMODULE bcd_submodule_15 (
    .in_1(bcd_submodule_9_out_8), .in_2(bcd_submodule_7_out_8), .in_3(bcd_submodule_5_out_8), .in_4(1'b0),
    .out_5(bcd_submodule_15_out_5), .out_6(bcd_submodule_15_out_6), .out_7(bcd_submodule_15_out_7),
    .out_8(bcd_submodule_15_out_8));
  BCD_SUBMODULE bcd_submodule_16 (
    .in_1(PROD_16[5]), .in_2(bcd_submodule_10_out_5), .in_3(bcd_submodule_10_out_6),
    .in_4(bcd_submodule_10_out_7), .out_5(bcd_submodule_16_out_5), .out_6(bcd_submodule_16_out_6),
    .out_7(bcd_submodule_16_out_7), .out_8(bcd_submodule_16_out_8));
  BCD_SUBMODULE bcd_submodule_17 (
    .in_1(bcd_submodule_10_out_8), .in_2(bcd_submodule_12_out_5), .in_3(bcd_submodule_12_out_6),
    .in_4(bcd_submodule_12_out_7), .out_5(bcd_submodule_17_out_5), .out_6(bcd_submodule_17_out_6),
    .out_7(bcd_submodule_17_out_7), .out_8(bcd_submodule_17_out_8));
  BCD_SUBMODULE bcd_submodule_18 (
    .in_1(bcd_submodule_12_out_8), .in_2(bcd_submodule_14_out_5), .in_3(bcd_submodule_14_out_6),
    .in_4(bcd_submodule_14_out_7), .out_5(bcd_submodule_18_out_5), .out_6(bcd_submodule_18_out_6),
    .out_7(bcd_submodule_18_out_7), .out_8(bcd_submodule_18_out_8));
  BCD_SUBMODULE bcd_submodule_19 (
    .in_1(PROD_16[4]), .in_2(bcd_submodule_16_out_5), .in_3(bcd_submodule_16_out_6),
    .in_4(bcd_submodule_16_out_7), .out_5(bcd_submodule_19_out_5), .out_6(bcd_submodule_19_out_6),
    .out_7(bcd_submodule_19_out_7), .out_8(bcd_submodule_19_out_8));
  BCD_SUBMODULE bcd_submodule_20 (
    .in_1(bcd_submodule_16_out_8), .in_2(bcd_submodule_17_out_5), .in_3(bcd_submodule_17_out_6),
    .in_4(bcd_submodule_17_out_7), .out_5(bcd_submodule_20_out_5), .out_6(bcd_submodule_20_out_6),
    .out_7(bcd_submodule_20_out_7), .out_8(bcd_submodule_20_out_8));
  BCD_SUBMODULE bcd_submodule_21 (
    .in_1(bcd_submodule_17_out_8), .in_2(bcd_submodule_18_out_5), .in_3(bcd_submodule_18_out_6),
    .in_4(bcd_submodule_18_out_7), .out_5(bcd_submodule_21_out_5), .out_6(bcd_submodule_21_out_6),
    .out_7(bcd_submodule_21_out_7), .out_8(bcd_submodule_21_out_8));
  BCD_SUBMODULE bcd_submodule_22 (
    .in_1(bcd_submodule_18_out_8), .in_2(bcd_submodule_14_out_8), .in_3(bcd_submodule_15_out_8), .in_4(1'b0),
    .out_5(bcd_submodule_22_out_5), .out_6(bcd_submodule_22_out_6), .out_7(bcd_submodule_22_out_7),
    .out_8(bcd_submodule_22_out_8));
  BCD_SUBMODULE bcd_submodule_23 (
    .in_1(PROD_16[3]), .in_2(bcd_submodule_19_out_5), .in_3(bcd_submodule_19_out_6),
    .in_4(bcd_submodule_19_out_7), .out_5(bcd_submodule_23_out_5), .out_6(bcd_submodule_23_out_6),
    .out_7(bcd_submodule_23_out_7), .out_8(bcd_submodule_23_out_8));
  BCD_SUBMODULE bcd_submodule_24 (
    .in_1(bcd_submodule_19_out_8), .in_2(bcd_submodule_20_out_5), .in_3(bcd_submodule_20_out_6),
    .in_4(bcd_submodule_20_out_7), .out_5(bcd_submodule_24_out_5), .out_6(bcd_submodule_24_out_6),
    .out_7(bcd_submodule_24_out_7), .out_8(bcd_submodule_24_out_8));
  BCD_SUBMODULE bcd_submodule_25 (
    .in_1(bcd_submodule_20_out_8), .in_2(bcd_submodule_21_out_5), .in_3(bcd_submodule_21_out_6),
    .in_4(bcd_submodule_21_out_7), .out_5(bcd_submodule_25_out_5), .out_6(bcd_submodule_25_out_6),
    .out_7(bcd_submodule_25_out_7), .out_8(bcd_submodule_25_out_8));
  BCD_SUBMODULE bcd_submodule_26 (
    .in_1(bcd_submodule_21_out_8), .in_2(bcd_submodule_22_out_5), .in_3(bcd_submodule_22_out_6),
    .in_4(bcd_submodule_22_out_7), .out_5(bcd_submodule_26_out_5), .out_6(bcd_submodule_26_out_6),
    .out_7(bcd_submodule_26_out_7), .out_8(bcd_submodule_26_out_8));
  BCD_SUBMODULE bcd_submodule_27 (
    .in_1(PROD_16[2]), .in_2(bcd_submodule_23_out_5), .in_3(bcd_submodule_23_out_6),
    .in_4(bcd_submodule_23_out_7), .out_5(bcd_submodule_27_out_5), .out_6(bcd_submodule_27_out_6),
    .out_7(bcd_submodule_27_out_7), .out_8(bcd_submodule_27_out_8));
  BCD_SUBMODULE bcd_submodule_28 (
    .in_1(bcd_submodule_23_out_8), .in_2(bcd_submodule_24_out_5), .in_3(bcd_submodule_24_out_6),
    .in_4(bcd_submodule_24_out_7), .out_5(bcd_submodule_28_out_5), .out_6(bcd_submodule_28_out_6),
    .out_7(bcd_submodule_28_out_7), .out_8(bcd_submodule_28_out_8));
  BCD_SUBMODULE bcd_submodule_29 (
    .in_1(bcd_submodule_24_out_8), .in_2(bcd_submodule_25_out_5), .in_3(bcd_submodule_25_out_6),
    .in_4(bcd_submodule_25_out_7), .out_5(bcd_submodule_29_out_5), .out_6(bcd_submodule_29_out_6),
    .out_7(bcd_submodule_29_out_7), .out_8(bcd_submodule_29_out_8));
  BCD_SUBMODULE bcd_submodule_30 (
    .in_1(bcd_submodule_25_out_8), .in_2(bcd_submodule_26_out_5), .in_3(bcd_submodule_26_out_6),
    .in_4(bcd_submodule_26_out_7), .out_5(bcd_submodule_30_out_5), .out_6(bcd_submodule_30_out_6),
    .out_7(bcd_submodule_30_out_7), .out_8(bcd_submodule_30_out_8));
  BCD_SUBMODULE bcd_submodule_31 (
    .in_1(bcd_submodule_29_out_8), .in_2(bcd_submodule_30_out_5), .in_3(bcd_submodule_30_out_6),
    .in_4(bcd_submodule_30_out_7), .out_5(FOURTH[1]), .out_6(FOURTH[2]), .out_7(FOURTH[3]), .out_8(FIFTH[0]));
  BCD_SUBMODULE bcd_submodule_32 (
    .in_1(bcd_submodule_30_out_8), .in_2(bcd_submodule_26_out_8), .in_3(bcd_submodule_22_out_8), .in_4(1'b0),
    .out_5(FIFTH[1]), .out_6(FIFTH[2]), .out_7(FIFTH[3]), .out_8(bcd_submodule_32_out_8));
  BCD_SUBMODULE bcd_submodule_33 (
    .in_1(PROD_16[1]), .in_2(bcd_submodule_27_out_5), .in_3(bcd_submodule_27_out_6),
    .in_4(bcd_submodule_27_out_7), .out_5(FIRST[1]), .out_6(FIRST[2]), .out_7(FIRST[3]), .out_8(SECOND[0]));
  BCD_SUBMODULE bcd_submodule_34 (
    .in_1(bcd_submodule_27_out_8), .in_2(bcd_submodule_28_out_5), .in_3(bcd_submodule_28_out_6),
    .in_4(bcd_submodule_28_out_7), .out_5(SECOND[1]), .out_6(SECOND[2]), .out_7(SECOND[3]), .out_8(THIRD[0]));
  BCD_SUBMODULE bcd_submodule_35 (
    .in_1(bcd_submodule_28_out_8), .in_2(bcd_submodule_29_out_5), .in_3(bcd_submodule_29_out_6),
    .in_4(bcd_submodule_29_out_7), .out_5(THIRD[1]), .out_6(THIRD[2]), .out_7(THIRD[3]), .out_8(FOURTH[0]));

  assign FIRST[0] = PROD_16[0];
  // also tied to GND on the sheet: bcd_submodule_32_out_8
endmodule

module CU (
  input  rst_crc,
  input  clk,
  input  shift_en,
  input  b0,
  input  [7:0] multiplier,
  output End_count,
  output load_en,
  output mux_sel,
  output zero_flag
);

  wire and_1_out, and_2_out, counter_2_q, not_1_out, not_2_out, not_3_out, not_4_out, not_6_out, or_1_out,
       or_2_out;
  wire [3:0] counter_1_q;

  and and_1 (and_1_out, shift_en, not_1_out);
  or or_1 (or_1_out, counter_2_q, b0);
  Counter #(.max('hf), .width(4)) counter_1 (
    .clr(rst_crc), .count(or_2_out), .clk(clk), .Q(counter_1_q));  // open: load, up, D, carry
  not not_1 (not_1_out, End_count);
  or or_2 (or_2_out, and_2_out, and_1_out);
  Counter #(.max('h1), .width(1)) counter_2 (
    .count(or_1_out), .Q(counter_2_q), .clk(clk), .clr(rst_crc));  // open: load, D, carry, up
  nor nor_1 (zero_flag, multiplier[0], multiplier[1], multiplier[2], multiplier[3], multiplier[4], multiplier[5], multiplier[6], multiplier[7]);
  not not_2 (not_2_out, counter_1_q[3]);
  not not_3 (not_3_out, counter_1_q[2]);
  not not_4 (not_4_out, counter_1_q[1]);
  and and_2 (and_2_out, not_2_out, not_3_out, not_4_out, not_6_out);
  not not_5 (mux_sel, and_2_out);
  not not_6 (not_6_out, counter_1_q[0]);
  and and_3 (End_count, counter_1_q[1], counter_1_q[3]);
  or or_3 (load_en, counter_2_q, and_2_out);
endmodule
